// Digital circuit Clock-driver.dig as structural Verilog
module Clock_driver (
  input  CLK_RAW,
  input  Stop,
  input  Run,
  input  One_Instruction,
  input  One_Step,
  input  One_Substep,
  input  nSTEPDONE,
  input  nOPDONE,
  input  nRESET,
  output CLK,
  output nCLK,
  output Running
);

  wire and_1_out, and_2_out, d_ff_as_1_q, d_ff_as_2_q, EN_CLK, nRAWCLK, pullup_1_out, pullup_2_out,
       pullup_3_out, pullup_4_out, pullup_5_out, rs_ff_as_1_q, rs_ff_as_2_q, rs_ff_as_3_q;

  PullUp pullup_1 (.out(pullup_1_out));
  PullUp pullup_2 (.out(pullup_2_out));
  PullUp pullup_3 (.out(pullup_3_out));
  PullUp pullup_4 (.out(pullup_4_out));
  DiodeBackward diodebackward_1 (.in(Stop), .out(pullup_2_out));
  DiodeBackward diodebackward_2 (.in(Stop), .out(pullup_3_out));
  DiodeBackward diodebackward_3 (.in(Stop), .out(pullup_4_out));
  not not_1 (nRAWCLK, CLK_RAW);
  DiodeBackward diodebackward_4 (.in(Run), .out(pullup_2_out));
  DiodeBackward diodebackward_5 (.in(Run), .out(pullup_3_out));
  DiodeBackward diodebackward_6 (.in(One_Instruction), .out(pullup_1_out));
  DiodeBackward diodebackward_7 (.in(One_Instruction), .out(pullup_2_out));
  DiodeBackward diodebackward_8 (.in(One_Instruction), .out(pullup_4_out));
  DiodeBackward diodebackward_9 (.in(One_Step), .out(pullup_1_out));
  DiodeBackward diodebackward_10 (.in(One_Step), .out(pullup_3_out));
  DiodeBackward diodebackward_11 (.in(One_Step), .out(pullup_4_out));
  DiodeBackward diodebackward_12 (.in(One_Substep), .out(pullup_1_out));
  DiodeBackward diodebackward_13 (.in(One_Substep), .out(pullup_2_out));
  DiodeBackward diodebackward_14 (.in(One_Substep), .out(pullup_3_out));
  DiodeBackward diodebackward_15 (.in(One_Substep), .out(pullup_4_out));
  D_FF_AS d_ff_as_1 (.Set(~nRESET), .D(1'b1), .C(nRAWCLK), .Clr(~pullup_1_out), .Q(d_ff_as_1_q));  // open: nQ
  RS_FF_AS rs_ff_as_1 (.S(~One_Step), .R(~pullup_2_out), .Q(rs_ff_as_1_q));  // open: nQ
  RS_FF_AS rs_ff_as_2 (.S(~One_Instruction), .R(~pullup_3_out), .Q(rs_ff_as_2_q));  // open: nQ
  RS_FF_AS rs_ff_as_3 (.S(~Run), .R(~pullup_4_out), .Q(rs_ff_as_3_q));  // open: nQ
  JK_FF jk_ff_1 (.J(EN_CLK), .C(CLK_RAW), .K(EN_CLK), .Q(CLK), .nQ(nCLK));
  PullUp pullup_5 (.out(pullup_5_out));
  DiodeBackward diodebackward_16 (.in(nRESET), .out(pullup_5_out));
  DiodeBackward diodebackward_17 (.in(nCLK), .out(pullup_5_out));
  D_FF_AS d_ff_as_2 (.Set(1'b0), .D(1'b1), .C(d_ff_as_1_q), .Clr(~pullup_5_out), .Q(d_ff_as_2_q));  // open: nQ
  and and_1 (and_1_out, rs_ff_as_1_q, nSTEPDONE);
  and and_2 (and_2_out, rs_ff_as_2_q, nOPDONE);
  DiodeForward diodeforward_1 (.in(d_ff_as_2_q), .out(Running));
  DiodeForward diodeforward_2 (.in(CLK), .out(Running));
  DiodeForward diodeforward_3 (.in(and_1_out), .out(Running));
  DiodeForward diodeforward_4 (.in(and_2_out), .out(Running));
  DiodeForward diodeforward_5 (.in(rs_ff_as_3_q), .out(Running));
  PullDown pulldown_1 (.out(Running));
  D_FF d_ff_1 (.D(Running), .C(nRAWCLK), .Q(EN_CLK));  // open: nQ

  // Other names for the same wires on the sheet: RAWCLK = CLK_RAW

  // Notes on the sheet:
  //   Stop: default 1
  //   Run: default 1
  //   One_Instruction: default 1
  //   One_Step: default 1
  //   One_Substep: default 1
  //   nSTEPDONE: default 1
  //   nOPDONE: default 1
endmodule
